// Logisim project DathaPath.circ as structural Verilog: 2 circuits, main circuit main
module main (
  input  [31:0] in_1,
  input  [31:0] in_2,
  input  [31:0] in_3,
  input  [31:0] in_4,
  input  CLK
);

  wire [31:0] PC_q, undriven;

  Register #(.width(32)) PC (.D(undriven), .Q(PC_q), .clk(CLK));  // open: en, clr
  Instruction_Data_Memory instruction_data_memory_1 (.in_3(PC_q));  // open: in_4, out_5, in_1, in_2

  // Other names for the same wires on the sheet: I0[31:0] = in_1; I1[31:0] = in_3; I2[31:0] = in_2; I3[31:0] = in_4
endmodule

module Instruction_Data_Memory (
  input  in_1,
  input  in_2,
  input  [31:0] in_3,
  input  [31:0] in_4,
  output [31:0] out_5
);


  // Other names for the same wires on the sheet: Address[31:0] = in_3; CLK = in_1; RD[31:0] = out_5; WD[31:0] = in_4;
  //   WE = in_2
endmodule
