// Logisim project Instruction Decoder.circ as structural Verilog: 1 circuit, main circuit Instruction Decoder
module Instruction_Decoder (
  input  [31:0] Instruction,
  output [25:0] out_2,
  output [4:0] out_3,
  output [4:0] out_4,
  output [4:0] out_5,
  output [15:0] out_6,
  output [5:0] out_7,
  output [5:0] out_8
);


  assign out_2 = Instruction[25:0];
  assign out_3 = Instruction[25:21];
  assign out_4 = Instruction[20:16];
  assign out_5 = Instruction[15:11];
  assign out_6 = Instruction[15:0];
  assign out_7 = Instruction[31:26];
  assign out_8 = Instruction[5:0];

  // Other names for the same wires on the sheet: Constante[15:0] = Instruction[15:0];
  //   Destino_Salto[25:0] = Instruction[25:0]; Func_code[5:0] = Instruction[5:0]; x[4:0] = Instruction[10:6];
  //   Rd[4:0] = Instruction[15:11]; Rt[4:0] = Instruction[20:16]; Rs[4:0] = Instruction[25:21];
  //   Op_Code[5:0] = Instruction[31:26]

  // Notes on the sheet:
  //   Instruction Decoder
  //   Outpout
endmodule
